# Fritzing sketch schematic (saved by Fritzing 0.7.10b)
breadboards: 1

parts:
  Arduino1 = Arduino
  K1 = Relay [part_number=FRS1B-S package=THT]
  Fuse1 = Fuse with Handler [part_number=Htc-15m]
  R1 = Photocell (LDR) [package=THT]  # not connected
  R2 = Photocell (LDR) [package=THT]  # not connected
  RHT1 = Humidity and Temperature Sensor RHT03  # not connected
  Part1 = Bluetooth Mate Silver
  L1 = Solenoid

nets:
  N1: Arduino1.D1TX, Part1.RX_5V
  N2: Arduino1.D0RX, Part1.TX_5V
  N3: K1.B, Fuse1.Connector1
  N4: Fuse1.Connector2, L1.pin2
